// Logisim project Project1Given.circ as structural Verilog: 4 circuits, main circuit main
module main (
  input  in_1,
  input  in_2,
  input  in_3,
  input  in_4,
  input  Five,
  output N,
  output E,
  output [3:0] out_8
);

  wire fiveseven_1_a, fiveseven_1_b, fiveseven_1_c, fiveseven_1_d, fiveseven_1_e, fiveseven_1_f,
       fiveseven_1_g;

  Compare compare_1 (.X0(1'b1), .X1(1'b0), .X2(1'b1), .Y0(1'b1), .Y1(1'b1), .Y2(1'b1), .N(N), .E(E));
  Gray gray_1 (.B0(1'b1), .B1(1'b0), .B2(1'b1), .B3(1'b1), .G0(out_8[0]), .G1(out_8[1]), .G2(out_8[2]), .G3(out_8[3]));
  FiveSeven fiveseven_1 (
    .V(in_1), .W(in_2), .X(in_3), .Y(in_4), .Z(Five), .A(fiveseven_1_a), .B(fiveseven_1_b),
    .C(fiveseven_1_c), .D(fiveseven_1_d), .E(fiveseven_1_e), .F(fiveseven_1_f), .G(fiveseven_1_g));
  _7_Segment_Display u_7_segment_display_1 (
    .g(fiveseven_1_g), .f(fiveseven_1_f), .a(fiveseven_1_a), .b(fiveseven_1_b), .e(fiveseven_1_e),
    .d(fiveseven_1_d), .c(fiveseven_1_c));  // open: dp
endmodule

module Compare (
  input  X0,
  input  X1,
  input  X2,
  input  Y0,
  input  Y1,
  input  Y2,
  output N,
  output E
);

  wire and_1_out, and_2_out, and_3_out, and_5_out, and_6_out, and_7_out, and_9_out, and_10_out, and_11_out,
       and_13_out, and_14_out, and_15_out, and_17_out, and_18_out, and_19_out, and_21_out, and_22_out,
       and_23_out, and_25_out, and_26_out, and_27_out, not_1_out, not_2_out, not_3_out, not_4_out, not_5_out,
       not_6_out, not_7_out, not_8_out, not_9_out, not_10_out, not_11_out, not_12_out, not_13_out,
       not_14_out, not_15_out, not_16_out, not_17_out, not_18_out, not_19_out, not_20_out, not_21_out,
       not_22_out, not_23_out, not_24_out, not_25_out, not_26_out, not_27_out, not_28_out, or_1_out,
       or_2_out, or_3_out, or_4_out, or_5_out, or_6_out, or_7_out, or_8_out;

  not not_1 (not_1_out, X2);
  not not_2 (not_2_out, Y2);
  not not_3 (not_3_out, X2);
  not not_4 (not_4_out, Y2);
  and and_1 (and_1_out, X2, Y2);
  and and_2 (and_2_out, not_1_out, not_2_out);
  and and_3 (and_3_out, not_3_out, Y2);
  // AND_Gate and_4 has open pins: in0=X2, in1=not_4_out, out=open
  not not_5 (not_5_out, X1);
  not not_6 (not_6_out, Y1);
  not not_7 (not_7_out, X1);
  not not_8 (not_8_out, Y1);
  not not_9 (not_9_out, X1);
  not not_10 (not_10_out, Y1);
  not not_11 (not_11_out, X1);
  not not_12 (not_12_out, Y1);
  and and_5 (and_5_out, X1, and_1_out, Y1);
  and and_6 (and_6_out, not_5_out, and_1_out, not_6_out);
  and and_7 (and_7_out, not_7_out, and_1_out, Y1);
  // AND_Gate and_8 has open pins: in0=X1, in1=and_1_out, in2=not_8_out, out=open
  and and_9 (and_9_out, X1, and_2_out, Y1);
  and and_10 (and_10_out, not_9_out, and_2_out, not_10_out);
  and and_11 (and_11_out, not_11_out, and_2_out, Y1);
  // AND_Gate and_12 has open pins: in0=X1, in1=and_2_out, in2=not_12_out, out=open
  not not_13 (not_13_out, X0);
  not not_14 (not_14_out, Y0);
  not not_15 (not_15_out, X0);
  not not_16 (not_16_out, Y0);
  not not_17 (not_17_out, X0);
  not not_18 (not_18_out, Y0);
  not not_19 (not_19_out, X0);
  not not_20 (not_20_out, Y0);
  not not_21 (not_21_out, X0);
  not not_22 (not_22_out, Y0);
  not not_23 (not_23_out, X0);
  not not_24 (not_24_out, Y0);
  not not_25 (not_25_out, X0);
  not not_26 (not_26_out, Y0);
  not not_27 (not_27_out, X0);
  not not_28 (not_28_out, Y0);
  and and_13 (and_13_out, X0, and_5_out, Y0);
  and and_14 (and_14_out, not_13_out, and_5_out, not_14_out);
  and and_15 (and_15_out, not_15_out, and_5_out, Y0);
  // AND_Gate and_16 has open pins: in0=X0, in1=and_5_out, in2=not_16_out, out=open
  and and_17 (and_17_out, X0, and_6_out, Y0);
  and and_18 (and_18_out, not_17_out, and_6_out, not_18_out);
  and and_19 (and_19_out, not_19_out, and_6_out, Y0);
  // AND_Gate and_20 has open pins: in0=X0, in1=and_6_out, in2=not_20_out, out=open
  and and_21 (and_21_out, X0, and_9_out, Y0);
  and and_22 (and_22_out, not_21_out, and_9_out, not_22_out);
  and and_23 (and_23_out, not_23_out, and_9_out, Y0);
  // AND_Gate and_24 has open pins: in0=X0, in1=and_9_out, in2=not_24_out, out=open
  and and_25 (and_25_out, X0, and_10_out, Y0);
  and and_26 (and_26_out, not_25_out, and_10_out, not_26_out);
  and and_27 (and_27_out, not_27_out, and_10_out, Y0);
  // AND_Gate and_28 has open pins: in0=X0, in1=and_10_out, in2=not_28_out, out=open
  or or_1 (or_1_out, and_13_out, and_14_out);
  or or_2 (or_2_out, and_17_out, and_18_out);
  or or_3 (or_3_out, and_21_out, and_22_out);
  or or_4 (or_4_out, and_25_out, and_26_out);
  or or_5 (or_5_out, and_15_out, and_19_out, and_7_out);
  or or_6 (or_6_out, and_23_out, and_27_out, and_11_out);
  or or_7 (or_7_out, or_1_out, or_2_out);
  or or_8 (or_8_out, or_3_out, or_4_out);
  or or_9 (E, or_7_out, or_8_out);
  or or_10 (N, or_5_out, or_6_out, and_3_out);

  // Other names for the same wires on the sheet: XequalsY = E; XLessThanY = N
endmodule

module Gray (
  input  B0,
  input  B1,
  input  B2,
  input  B3,
  output G0,
  output G1,
  output G2,
  output G3
);

  wire and_1_out, and_2_out, and_3_out, and_4_out, and_5_out, and_6_out, and_7_out, and_8_out, and_9_out,
       and_10_out, and_11_out, not_1_out, not_2_out, not_3_out, not_4_out, not_5_out, not_6_out, not_7_out,
       not_8_out, not_9_out, not_10_out, not_11_out, not_12_out, not_13_out, not_14_out, not_15_out,
       not_16_out, not_17_out;

  not not_1 (not_1_out, B2);
  not not_2 (not_2_out, B1);
  not not_3 (not_3_out, B0);
  not not_4 (not_4_out, B3);
  not not_5 (not_5_out, B3);
  not not_6 (not_6_out, B3);
  not not_7 (not_7_out, B3);
  not not_8 (not_8_out, B2);
  not not_9 (not_9_out, B3);
  not not_10 (not_10_out, B2);
  not not_11 (not_11_out, B2);
  not not_12 (not_12_out, B1);
  not not_13 (not_13_out, B0);
  and and_1 (and_1_out, B3, not_1_out);
  and and_2 (and_2_out, B3, not_2_out, not_3_out);
  and and_3 (and_3_out, not_4_out, B2, B1);
  and and_4 (and_4_out, not_5_out, B2, B0);
  and and_5 (and_5_out, not_6_out, B2);
  and and_6 (and_6_out, not_7_out, not_8_out, B1);
  and and_7 (and_7_out, not_9_out, not_10_out, B0);
  and and_8 (and_8_out, B3, not_11_out, not_12_out, not_13_out);
  or or_1 (G3, and_1_out, and_2_out, and_3_out, and_4_out);
  or or_2 (G2, and_5_out, and_6_out, and_7_out, and_8_out);
  not not_14 (not_14_out, B2);
  not not_15 (not_15_out, B0);
  and and_9 (and_9_out, B2, B1, B0);
  not not_16 (not_16_out, B2);
  not not_17 (not_17_out, B1);
  and and_10 (and_10_out, not_14_out, B1, not_15_out);
  and and_11 (and_11_out, not_16_out, not_17_out);
  or or_3 (G1, and_9_out, and_11_out, and_10_out);

  assign G0 = B1;
endmodule

module FiveSeven (
  input  V,
  input  W,
  input  X,
  input  Y,
  input  Z,
  output A,
  output B,
  output C,
  output D,
  output E,
  output F,
  output G
);

  wire and_1_out, and_2_out, and_3_out, and_4_out, and_5_out, and_6_out, and_7_out, and_8_out, and_9_out,
       and_10_out, and_11_out, and_13_out, and_14_out, and_15_out, and_16_out, and_17_out, and_18_out,
       and_19_out, and_20_out, and_21_out, and_22_out, and_23_out, L0, L1, L2, L3, L4, L5, L6, L7, L8, L9,
       nor_1_out, not_1_out, not_2_out, not_3_out, not_4_out, not_5_out, not_6_out, not_7_out, not_8_out,
       not_9_out, not_10_out, not_11_out, not_12_out, not_13_out, not_14_out, not_15_out, not_16_out,
       not_17_out, not_18_out, not_19_out, not_20_out, not_21_out, not_22_out, not_23_out, not_24_out,
       not_25_out, not_26_out, not_27_out, not_28_out, not_29_out, not_30_out, not_31_out, not_32_out,
       not_33_out, not_34_out, not_35_out, not_36_out, not_37_out, not_38_out, not_39_out, not_40_out,
       not_41_out, or_1_out, or_2_out, or_3_out, or_4_out, or_5_out, or_6_out, or_7_out, or_8_out, xor_1_out,
       xor_2_out;

  not not_1 (not_1_out, Z);
  not not_2 (not_2_out, Z);
  not not_3 (not_3_out, X);
  not not_4 (not_4_out, Y);
  not not_5 (not_5_out, W);
  not not_6 (not_6_out, Y);
  not not_7 (not_7_out, W);
  not not_8 (not_8_out, X);
  not not_9 (not_9_out, V);
  not not_10 (not_10_out, Y);
  not not_11 (not_11_out, V);
  not not_12 (not_12_out, X);
  not not_13 (not_13_out, V);
  not not_14 (not_14_out, W);
  not not_15 (not_15_out, Z);
  not not_16 (not_16_out, Y);
  not not_17 (not_17_out, X);
  not not_18 (not_18_out, W);
  not not_19 (not_19_out, V);
  not not_20 (not_20_out, Z);
  not not_21 (not_21_out, Z);
  not not_22 (not_22_out, L6);
  not not_23 (not_23_out, L7);
  not not_24 (not_24_out, L8);
  not not_25 (not_25_out, L9);
  not not_26 (not_26_out, X);
  not not_27 (not_27_out, Y);
  not not_28 (not_28_out, W);
  not not_29 (not_29_out, Y);
  not not_30 (not_30_out, W);
  not not_31 (not_31_out, X);
  not not_32 (not_32_out, V);
  not not_33 (not_33_out, Y);
  not not_34 (not_34_out, V);
  not not_35 (not_35_out, X);
  not not_36 (not_36_out, V);
  not not_37 (not_37_out, W);
  not not_38 (not_38_out, Y);
  not not_39 (not_39_out, X);
  not not_40 (not_40_out, W);
  not not_41 (not_41_out, V);
  nor nor_1 (nor_1_out, V, W, X, Y);
  ExactlyOne xor_1 (.out(xor_1_out), .in0(V), .in1(W), .in2(X), .in3(Y));
  and and_1 (and_1_out, V, W, not_3_out, not_4_out);
  and and_2 (and_2_out, V, not_5_out, X, not_6_out);
  and and_3 (and_3_out, V, not_7_out, not_8_out, Y);
  and and_4 (and_4_out, not_9_out, W, X, not_10_out);
  and and_5 (and_5_out, not_11_out, W, not_12_out, Y);
  and and_6 (and_6_out, not_13_out, not_14_out, X, Y);
  and and_7 (and_7_out, V, W, X, not_16_out);
  and and_8 (and_8_out, V, W, not_17_out, Y);
  and and_9 (and_9_out, V, not_18_out, X, Y);
  and and_10 (and_10_out, not_19_out, W, X, Y);
  and and_11 (and_11_out, V, W, X, Y);
  and and_12 (L5, Z, not_22_out, not_23_out, not_24_out, not_25_out);
  ExactlyOne xor_2 (.out(xor_2_out), .in0(V), .in1(W), .in2(X), .in3(Y));
  and and_13 (and_13_out, V, W, not_26_out, not_27_out);
  and and_14 (and_14_out, V, not_28_out, X, not_29_out);
  and and_15 (and_15_out, V, not_30_out, not_31_out, Y);
  and and_16 (and_16_out, not_32_out, W, X, not_33_out);
  and and_17 (and_17_out, not_34_out, W, not_35_out, Y);
  and and_18 (and_18_out, not_36_out, not_37_out, X, Y);
  and and_19 (and_19_out, V, W, X, not_38_out);
  and and_20 (and_20_out, V, W, not_39_out, Y);
  and and_21 (and_21_out, V, not_40_out, X, Y);
  and and_22 (and_22_out, not_41_out, W, X, Y);
  and and_23 (and_23_out, V, W, X, Y);
  and and_24 (L0, nor_1_out, not_1_out);
  and and_25 (L1, xor_1_out, not_2_out);
  and and_26 (L4, and_11_out, not_21_out);
  and and_27 (L6, Z, xor_2_out);
  and and_28 (L9, Z, and_23_out);
  or or_1 (or_1_out, and_1_out, and_2_out, and_3_out);
  or or_2 (or_2_out, and_4_out, and_5_out, and_6_out);
  or or_3 (or_3_out, and_13_out, and_14_out, and_15_out);
  or or_4 (or_4_out, and_7_out, and_8_out, and_9_out, and_10_out);
  or or_5 (or_5_out, and_16_out, and_17_out, and_18_out);
  or or_6 (or_6_out, and_19_out, and_20_out, and_21_out, and_22_out);
  or or_7 (or_7_out, or_1_out, or_2_out);
  and and_29 (L3, or_4_out, not_20_out);
  or or_8 (or_8_out, or_3_out, or_5_out);
  and and_30 (L8, Z, or_6_out);
  and and_31 (L2, or_7_out, not_15_out);
  and and_32 (L7, Z, or_8_out);
  or or_9 (E, L0, L2, L6, L8);
  or or_10 (C, L0, L1, L3, L4, L5, L6, L7, L8, L9);
  or or_11 (D, L0, L2, L3, L5, L6, L8, L9);
  or or_12 (F, L0, L4, L5, L6, L8, L9);
  or or_13 (G, L2, L3, L4, L5, L6, L8, L9);
  or or_14 (A, L0, L2, L3, L5, L6, L7, L8, L9);
  or or_15 (B, L0, L1, L2, L3, L4, L7, L8, L9);
endmodule
